# Fritzing sketch fritzing_sketch (saved by Fritzing 0.9.3b)
circuit board: 9.33863cm x 6.70622cm
breadboards: 1

parts:
  IC2 = H-Bridge [package=THT]
  RPi = Raspberry Pi 3 [part_number=RPI-3-V1.2]
  M2 = Stepper Motor - Unipolar
  IC3 = H-Bridge [package=THT]
  M3 = Stepper Motor - Unipolar
  MCP2 = IC, DIP package, 16 pins [chip_label=MCP3008]
  J3 = Infrared Proximity Sensor
  J4 = Infrared Proximity Sensor
  J5 = Infrared Proximity Sensor
  J6 = Infrared Proximity Sensor
  J7 = Infrared Proximity Sensor
  J8 = Infrared Proximity Sensor
  J9 = Infrared Proximity Sensor
  J10 = Infrared Proximity Sensor
  J11 = Infrared Proximity Sensor
  J12 = Infrared Proximity Sensor
  J13 = Infrared Proximity Sensor
  J14 = Infrared Proximity Sensor
  J15 = Infrared Proximity Sensor
  J16 = Infrared Proximity Sensor
  J17 = Infrared Proximity Sensor
  J18 = Infrared Proximity Sensor
  J19 = Infrared Proximity Sensor
  J20 = Infrared Proximity Sensor
  J21 = Infrared Proximity Sensor
  J22 = Infrared Proximity Sensor
  J23 = Infrared Proximity Sensor
  J24 = Infrared Proximity Sensor
  J25 = Infrared Proximity Sensor
  J26 = Infrared Proximity Sensor
  MCP3 = IC, DIP package, 16 pins [chip_label=MCP3008]
  MCP1 = IC, DIP package, 16 pins [chip_label=MCP3008]

nets:
  N1: IC2.1_2EN, IC2.VCC2, IC2.3_4EN, IC2.VCC1, IC3.1_2EN, IC3.VCC2, IC3.3_4EN, IC3.VCC1
  N2: IC2.1A, RPi.GPIO26
  N3: IC2.1Y, M2.A
  GND: IC2.GND1, IC2.GND2, IC2.GND3, IC2.GND4, RPi.GND, IC3.GND1, IC3.GND2, IC3.GND3, IC3.GND4, MCP2.pin9, MCP2.pin14, J3.GND, J4.GND, J5.GND, J6.GND, J7.GND, J8.GND, J9.GND, J10.GND, J11.GND, J12.GND, J13.GND, J14.GND, J15.GND, J16.GND, J17.GND, J18.GND, J19.GND, J20.GND, J21.GND, J22.GND, J23.GND, J24.GND, J25.GND, J26.GND, MCP3.pin9, MCP3.pin14, MCP1.pin9, MCP1.pin14
  N4: IC2.2Y, M2.C
  N5: IC2.2A, RPi.GPIO19
  N6: IC2.3A, RPi.GPIO6
  N7: IC2.3Y, M2.D
  N8: IC2.4Y, M2.B
  N9: IC2.4A, RPi.GPIO13
  3V3: RPi.3v3, RPi.3V3, MCP2.pin15, MCP2.pin16, MCP3.pin15, MCP3.pin16, MCP1.pin15, MCP1.pin16
  N10: RPi.GPIO17, MCP1.pin10
  N11: RPi.GPIO27, MCP2.pin10
  N12: RPi.GPIO22, MCP3.pin10
  N13: RPi.GPIO10, MCP2.pin11, MCP3.pin11, MCP1.pin11
  N14: RPi.GPIO9, MCP2.pin12, MCP3.pin12, MCP1.pin12
  N15: RPi.GPIO11, MCP2.pin13, MCP3.pin13, MCP1.pin13
  N16: RPi.GPIO21, IC3.1A
  N17: RPi.GPIO20, IC3.2A
  N18: RPi.GPIO16, IC3.4A
  N19: RPi.GPIO12, IC3.3A
  VCC: RPi.5V, J3.Vcc, J4.Vcc, J5.Vcc, J6.Vcc, J7.Vcc, J8.Vcc, J9.Vcc, J10.Vcc, J11.Vcc, J12.Vcc, J13.Vcc, J14.Vcc, J15.Vcc, J16.Vcc, J17.Vcc, J18.Vcc, J19.Vcc, J20.Vcc, J21.Vcc, J22.Vcc, J23.Vcc, J24.Vcc, J25.Vcc, J26.Vcc
  N20: IC3.1Y, M3.A
  N21: IC3.2Y, M3.C
  N22: IC3.3Y, M3.D
  N23: IC3.4Y, M3.B
  N24: MCP2.pin1, J12.Vout
  N25: MCP2.pin2, J17.Vout
  N26: MCP2.pin3, J16.Vout
  N27: MCP2.pin4, J13.Vout
  N28: MCP2.pin5, J11.Vout
  N29: MCP2.pin6, J15.Vout
  N30: MCP2.pin7, J14.Vout
  N31: MCP2.pin8, J18.Vout
  N32: J3.Vout, MCP1.pin8
  N33: J4.Vout, MCP1.pin7
  N34: J5.Vout, MCP1.pin6
  N35: J6.Vout, MCP1.pin5
  N36: J7.Vout, MCP1.pin4
  N37: J8.Vout, MCP1.pin3
  N38: J9.Vout, MCP1.pin2
  N39: J10.Vout, MCP1.pin1
  N40: J19.Vout, MCP3.pin7
  N41: J20.Vout, MCP3.pin4
  N42: J21.Vout, MCP3.pin3
  N43: J22.Vout, MCP3.pin6
  N44: J23.Vout, MCP3.pin1
  N45: J24.Vout, MCP3.pin8
  N46: J25.Vout, MCP3.pin2
  N47: J26.Vout, MCP3.pin5

notes:
  GPIO05 - Mot2_D
  GPIO06 - Mot2_B
  GPIO13 - Mot2_C
  GPIO19 - Mot2_A
  GPIO12 - Mot1_D
  GPIO16 - Mot1_B
  GPIO20 - Mot1_C
  GPIO21 - Mot1_A
  CLK - SPI_CLK
  D_IN - SPI_MOSI
  D_OUT - SPI_MISO
  Mcp1_CS - GPIO17
  Mcp2_CS - GPIO27
  Mcp3_CS - GPIO22
